# Fritzing sketch Fan (saved by Fritzing 1.0.2b)
breadboards: 1

parts:
  Q1 = NPN-Transistor [package="TO92 [THT]"]
  M1 = DC Motor [voltage_(max)=6V voltage_(min)=3V]
  D1 = Schottky Diode [part_number=1N5817 package="Melf DO-213 AB [SMD]"]
  Mod1 = Raspberry Pi Pico

nets:
  N1: Q1.E, Mod1.pin_23, Mod1.pin_33
  N2: Q1.B, Mod1.pin_14
  N3: Q1.C, M1.pin_2, D1.anode
  N4: M1.pin_1, D1.cathode, Mod1.pin_40

custom parts:
  Raspberry Pi Pico: Raspberry Pi Pico. Based around the RP2040 microcontroller the Pico is a low cost microcontroller device bringing Raspberry Pi quality, cost, and easy of use to the microcontroller space. Jan 2021, Split part in to two versions: tht (this one) and SMD. This one will drill holes for a .1 in header in pcb to allow plugging in the module as well as providing pads to solder the module to the top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
